// Logisim project cpu.circ as structural Verilog: 1 circuit, main circuit main
module main (
);

  wire button_1_out, clock_1_out, comparator_1_eq, comparator_1_lt, comparator_2_eq, comparator_3_eq,
       comparator_4_eq, nand_1_out, not_1_out, not_2_out, or_1_out, or_2_out, pull_resistor_1_node,
       rom_2_data;
  wire [1:0] Inst_Phase_q, pull_resistor_3_node;
  wire [3:0] pull_resistor_2_node, pull_resistor_2_node_2;
  wire [7:0] A2_q, A_q, adder_1_out, B2_q, B_q, counter_1_q, Instruction_q, Operand_q, pull_resistor_5_node,
       ram_1_data, subtractor_1_out, subtractor_2_out;
  wire [7:7] pull_resistor_5_node_2;
  wire [15:0] pull_resistor_4_node, rom_3_data;

  Pull_Resistor pull_resistor_1 (.node(pull_resistor_1_node));
  assign pull_resistor_1_node = not_1_out ? clock_1_out : 1'bz;  // Controlled_Buffer controlled_buffer_1
  Clock clock_1 (.out(clock_1_out));
  not not_1 (not_1_out, button_1_out);
  Button button_1 (.out(button_1_out));
  Pull_Resistor pull_resistor_2 (.node({pull_resistor_2_node_2, pull_resistor_2_node}));
  Pull_Resistor pull_resistor_3 (.node(pull_resistor_3_node));
  Pull_Resistor pull_resistor_4 (.node(pull_resistor_4_node));
  Pull_Resistor pull_resistor_5 (.node({pull_resistor_5_node_2[7], pull_resistor_5_node[6:0]}));
  Counter #(.width(2), .max('h3), .trigger("falling")) Inst_Phase (
    .Q(Inst_Phase_q), .clk(pull_resistor_1_node), .clr(button_1_out));  // open: load, D, count, carry
  Comparator #(.width(2), .mode("unsigned")) comparator_1 (
    .a(Inst_Phase_q), .b(2'b01), .eq(comparator_1_eq), .lt(comparator_1_lt));  // open: gt
  or or_1 (or_1_out, comparator_1_eq, comparator_1_lt);
  or or_2 (or_2_out, or_1_out, pull_resistor_4_node[10]);
  Pull_Resistor pull_resistor_6 (.node(pull_resistor_5_node));
  Counter counter_1 (
    .load(pull_resistor_4_node[10]), .D({pull_resistor_2_node_2, pull_resistor_2_node}), .count(or_1_out),
    .Q(counter_1_q), .clk(nand_1_out), .clr(button_1_out));  // open: carry
  nand nand_1 (nand_1_out, or_2_out, pull_resistor_1_node);
  assign {pull_resistor_5_node_2[7], pull_resistor_5_node[6:0]} = or_1_out ? counter_1_q : 8'bz;  // Controlled_Buffer controlled_buffer_2
  assign {pull_resistor_2_node_2, pull_resistor_2_node} = pull_resistor_4_node[9] ? counter_1_q : 8'bz;  // Controlled_Buffer controlled_buffer_3
  assign {pull_resistor_2_node_2, pull_resistor_2_node} = pull_resistor_4_node[7] ? ram_1_data : 8'bz;  // Controlled_Buffer controlled_buffer_4
  Comparator #(.width(2)) comparator_2 (.a(Inst_Phase_q), .b(2'b00), .eq(comparator_2_eq));  // open: gt, lt
  assign pull_resistor_4_node = or_1_out ? 16'h80 : 16'bz;  // Controlled_Buffer controlled_buffer_5
  Register Instruction (
    .D({pull_resistor_2_node_2, pull_resistor_2_node}), .en(comparator_2_eq), .Q(Instruction_q),
    .clk(pull_resistor_1_node), .clr(button_1_out));
  RAM #(.bus("separate")) ram_1 (
    .addr(pull_resistor_5_node), .din({pull_resistor_2_node_2, pull_resistor_2_node}), .data(ram_1_data),
    .str(pull_resistor_4_node[8]), .sel(pull_resistor_5_node_2[7]), .clk(pull_resistor_1_node), .ld(1'b1),
    .clr(button_1_out));
  Comparator #(.width(2)) comparator_3 (.a(Inst_Phase_q), .b(2'b01), .eq(comparator_3_eq));  // open: gt, lt
  not not_2 (not_2_out, pull_resistor_5_node_2[7]);
  Register Operand (
    .D({pull_resistor_2_node_2, pull_resistor_2_node}), .en(comparator_3_eq), .Q(Operand_q),
    .clk(pull_resistor_1_node), .clr(button_1_out));
  assign {pull_resistor_2_node_2, pull_resistor_2_node} = pull_resistor_4_node[11] ? Operand_q : 8'bz;  // Controlled_Buffer controlled_buffer_6
  assign {pull_resistor_5_node_2[7], pull_resistor_5_node[6:0]} = pull_resistor_4_node[12] ? Operand_q : 8'bz;  // Controlled_Buffer controlled_buffer_7
  ROM rom_1 (.addr(pull_resistor_5_node), .data(ram_1_data), .sel(not_2_out));
  Hex_Digit_Display hex_digit_display_1 (.value({pull_resistor_5_node_2[7], pull_resistor_5_node[6:4]}));  // open: dp
  Hex_Digit_Display hex_digit_display_2 (.value(pull_resistor_5_node[3:0]));  // open: dp
  ROM #(.addrWidth(4), .dataWidth(1)) rom_2 (
    .addr({pull_resistor_3_node, Instruction_q[6], Instruction_q[7]}), .data(rom_2_data));  // open: sel
  ROM #(.addrWidth(7), .dataWidth(16)) rom_3 (
    .addr({Instruction_q[5:0], Inst_Phase_q[0]}), .data(rom_3_data), .sel(Inst_Phase_q[1]));
  assign pull_resistor_4_node = rom_2_data ? rom_3_data : 16'bz;  // Controlled_Buffer controlled_buffer_8
  Hex_Digit_Display hex_digit_display_3 (.value(pull_resistor_2_node_2));  // open: dp
  Hex_Digit_Display hex_digit_display_4 (.value(pull_resistor_2_node));  // open: dp
  TTY tty_1 (
    .data({pull_resistor_2_node_2[2:0], pull_resistor_2_node}), .clk(pull_resistor_1_node),
    .we(comparator_4_eq), .clr(button_1_out));
  Comparator comparator_4 (
    .a({pull_resistor_5_node_2[7], pull_resistor_5_node[6:0]}), .b({8{1'b1}}), .eq(comparator_4_eq));  // open: gt, lt
  Register A (
    .D({pull_resistor_2_node_2, pull_resistor_2_node}), .en(pull_resistor_4_node[1]), .Q(A_q),
    .clk(pull_resistor_1_node), .clr(button_1_out));
  assign {pull_resistor_5_node_2[7], pull_resistor_5_node[6:0]} = pull_resistor_4_node[13] ? A_q : 8'bz;  // Controlled_Buffer controlled_buffer_9
  assign {pull_resistor_2_node_2, pull_resistor_2_node} = pull_resistor_4_node[0] ? A_q : 8'bz;  // Controlled_Buffer controlled_buffer_10
  Register B (
    .D({pull_resistor_2_node_2, pull_resistor_2_node}), .en(pull_resistor_4_node[3]), .Q(B_q),
    .clk(pull_resistor_1_node), .clr(button_1_out));
  assign {pull_resistor_5_node_2[7], pull_resistor_5_node[6:0]} = pull_resistor_4_node[14] ? B_q : 8'bz;  // Controlled_Buffer controlled_buffer_11
  assign {pull_resistor_2_node_2, pull_resistor_2_node} = pull_resistor_4_node[2] ? B_q : 8'bz;  // Controlled_Buffer controlled_buffer_12
  Register A2 (.D(A_q), .en(pull_resistor_4_node[15]), .Q(A2_q), .clk(pull_resistor_1_node), .clr(button_1_out));
  Register B2 (.D(B_q), .en(pull_resistor_4_node[15]), .Q(B2_q), .clk(pull_resistor_1_node), .clr(button_1_out));
  Adder adder_1 (.a(A2_q), .b(B2_q), .out(adder_1_out));  // open: cin, cout
  assign {pull_resistor_2_node_2, pull_resistor_2_node} = pull_resistor_4_node[4] ? adder_1_out : 8'bz;  // Controlled_Buffer controlled_buffer_13
  Subtractor subtractor_1 (.a(A2_q), .b(B2_q), .out(subtractor_1_out));  // open: bin, bout
  assign {pull_resistor_2_node_2, pull_resistor_2_node} = pull_resistor_4_node[5] ? subtractor_1_out : 8'bz;  // Controlled_Buffer controlled_buffer_14
  Subtractor subtractor_2 (.a(B2_q), .b(A2_q), .out(subtractor_2_out));  // open: bin, bout
  assign {pull_resistor_2_node_2, pull_resistor_2_node} = pull_resistor_4_node[6] ? subtractor_2_out : 8'bz;  // Controlled_Buffer controlled_buffer_15
  or or_3 (pull_resistor_3_node[0], A_q[0], A_q[1], A_q[2], A_q[3], A_q[4], A_q[5], A_q[6], A_q[7]);
  or or_4 (pull_resistor_3_node[1], B_q[0], B_q[1], B_q[2], B_q[3], B_q[4], B_q[5], B_q[6], B_q[7]);

  // Notes on the sheet:
  //   Clock
  //   Data Bus
  //   Control Bus
  //   Address Bus
  //   Flags Bus
  //   Reset
  //   PC
  //   Instruction Fetch
  //   contents of rom_1 (hex, n*v repeats v):
  //   d f c 1 5 0 14 0 a ff 50 2 10 c 0 0 68 65 6c 6c 6f
  //   bad hack to flip bits
  //   Conditional Check
  //   Microcode
  //   Address
  //   contents of rom_2 (hex, n*v repeats v):
  //   1 0 0 1 1 0 4*1 0 5*1
  //   contents of rom_3 (hex, n*v repeats v):
  //   0 0 6 0 9 0 0 0 8000 12 8000 18 8000 22 8000 48 1082 0 1088 0 1101 0 1104 0 802 0 808 0 401 401 404
  //   404 c00 c00 6*0 4082 0 2088 0 4101 0 2104
  //   Data
  //   Registers
  //   Shadow Registers
  //   ALU
endmodule
